# Fritzing sketch v1 (saved by Fritzing 0.9.2b)
breadboards: 1

parts:
  C1 = Electrolytic Capacitor [capacitance=1mF package="200 mil [THT, electrolytic]"]
  Part1 = Itsy Bitsy M0 Express
  Part2 = Adafruit DS3231 [part_number="Adafruit #3013"]
  R1 = Resistor [tolerance=±5% resistance=470 package=THT]
  NEOPIXEL1 = Neopixel Strip -- Black (60/m)

nets:
  GND: C1.-, Part1.GND, Part2.GND, NEOPIXEL1.GND
  N1: C1.+, Part1.VHI, NEOPIXEL1.+5V
  N2: Part1.D5_5V, R1.Pin_1
  N3: Part1.SCL, Part2.SCL
  N4: Part1.SDA, Part2.SDA
  +3V3: Part1.+3V3, Part2.Vin
  N5: R1.Pin_0, NEOPIXEL1.DI

custom parts:
  Itsy Bitsy M0 Express: What's smaller than a Feather but larger than a Trinket? It's an Adafruit ItsyBitsy M0 Express! Small, powerful, with a rockin' ATSAMD21 Cortex M0 processor running at 48 MHz - this microcontroller board is perfect when you want something very compact, but still with a bunch of pins. ItsyBitsy M0 Express is only 1.4" long by 0.7" wide, but has 6 power pins, 23 digital GPIO pins (12 of which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
  Adafruit DS3231: The datasheet for the DS3231 explains that this part is an "Extremely Accurate I²C-Integrated RTC/TCXO/Crystal". And, hey, it does exactly what it says on the tin! This Real Time Clock (RTC) is the most precise you can get in a small, low power package. Most RTCs use an external 32kHz timing crystal that is used to keep time with low current draw. And that's all well and good, but those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
  Neopixel Strip -- Black (60/m): Neopixel Strip, Black, 60 pixels per meter.
